# Fritzing sketch circuit (saved by Fritzing 0.9.4)
breadboards: 1

parts:
  U1 = NodeMCU V3.0
  JACK1 = 2.1mm Barrel Jack with Terminal Block
  U2 = TRANSISTOR_NPN_2 [package=to-92]
  U3 = TRANSISTOR_NPN_2 [package=to-92]
  U4 = TRANSISTOR_NPN_2 [package=to-92]
  U5 = TRANSISTOR_NPN_2 [package=to-92]
  U6 = TRANSISTOR_NPN_2 [package=to-92]
  IC1 = Voltage Regulator [package=to220-igo]
  R1 = Resistor [tolerance=±5% resistance=220 package=THT]
  R2 = Resistor [tolerance=±5% resistance=220 package=THT]
  R3 = Resistor [tolerance=±5% resistance=220 package=THT]
  R4 = Resistor [tolerance=±5% resistance=220 package=THT]
  R5 = Resistor [tolerance=±5% resistance=220 package=THT]
  C1 = Electrolytic Capacitor [capacitance=1000μF package="1010 [SMD, electrolytic]"]
  C2 = Electrolytic Capacitor [capacitance=1000μF package="1010 [SMD, electrolytic]"]

nets:
  N1: U1.D1, R1.Pin_1
  N2: U1.D5, R2.Pin_1
  N3: U1.D6, R3.Pin_1
  N4: U1.D7, R4.Pin_1
  N5: U1.D8, R5.Pin_1
  N6: U1.GND, IC1.IN, C1.-, C2.-
  N7: U1.Vin, IC1.OUT, C1.+
  N8: JACK1.NEG, U2.C, U3.C, U4.C, U5.C, U6.C
  N9: U2.B, R1.Pin_0
  N10: U3.B, R2.Pin_0
  N11: U4.B, R3.Pin_0
  N12: U5.B, R4.Pin_0
  N13: U6.B, R5.Pin_0
  N14: IC1.GND, C2.+

notes:
  12V R G B W Y
  LED STRIP

custom parts:
  NodeMCU V3.0: ESP8266 based NodeMCU
