# Fritzing sketch transistor_led (saved by Fritzing 0.9.4)
breadboards: 1

parts:
  U1 = NodeMCU V3.0
  U2 = TRANSISTOR_NPN_2 [package=to-92]
  R1 = Resistor [tolerance=±5% resistance=220 package=THT]

nets:
  N1: U1.D1, R1.Pin_1
  N2: U2.B, R1.Pin_0

custom parts:
  NodeMCU V3.0: ESP8266 based NodeMCU
