# Fritzing sketch voltage_regulator_circuit (saved by Fritzing 0.9.4)
breadboards: 1

parts:
  U1 = NodeMCU V3.0
  JACK1 = 2.1mm Barrel Jack with Terminal Block  # not connected
  IC1 = Voltage Regulator [package=to220-igo]
  C1 = Electrolytic Capacitor [capacitance=1000μF package="1010 [SMD, electrolytic]"]
  C2 = Electrolytic Capacitor [capacitance=1000μF package="1010 [SMD, electrolytic]"]

nets:
  N1: U1.GND, IC1.IN, C1.-, C2.-
  N2: U1.Vin, IC1.OUT, C1.+
  N3: IC1.GND, C2.+

custom parts:
  NodeMCU V3.0: ESP8266 based NodeMCU
